// Logisim project  xhuang78_project1.circ as structural Verilog: 2 circuits, main circuit main
module main (
  output Clock,
  output State,
  output R1,
  output Y1,
  output G1,
  output R2,
  output Y2,
  output halt,
  output G2
);

  wire Clock_out;
  wire [6:1] counter_1_q;

  Clock u_Clock (.out(Clock_out));
  Counter #(.width(7), .max('h7f)) counter_1 (
    .Q({counter_1_q[6:4], State, counter_1_q[2:1], Clock}), .carry(halt), .clk(Clock_out));  // open: load, D, count, clr
  Traffic_Light traffic_light_1 (.State(State), .Clock(Clock), .R1(R1), .Y1(Y1), .G1(G1), .R2(R2), .Y2(Y2), .G2(G2));
endmodule

module Traffic_Light (
  input  State,
  input  Clock,
  output R1,
  output Y1,
  output G1,
  output R2,
  output Y2,
  output G2
);

  wire _000_out, _001_out, _010_out, _011_out, _100_out, _101_out, _110_out, _111_out, d_ff_1_q, d_ff_2_q,
       d_ff_3_q, d_ff_4_q, d_ff_5_q, d_ff_6_q, not_1_out, or_4_out, or_5_out, or_6_out;

  and _000 (_000_out, ~d_ff_1_q, ~d_ff_2_q, ~d_ff_3_q);  // AND_Gate
  and _001 (_001_out, ~d_ff_1_q, ~d_ff_2_q, d_ff_3_q, ~State);  // AND_Gate
  and _010 (_010_out, ~d_ff_1_q, d_ff_2_q, ~d_ff_3_q, ~State);  // AND_Gate
  and _011 (_011_out, ~d_ff_1_q, d_ff_2_q, d_ff_3_q);  // AND_Gate
  and _100 (_100_out, d_ff_1_q, ~d_ff_2_q, ~d_ff_3_q, State);  // AND_Gate
  and _101 (_101_out, d_ff_1_q, ~d_ff_2_q, d_ff_3_q, State);  // AND_Gate
  and _110 (_110_out, d_ff_1_q, d_ff_2_q, ~d_ff_3_q, State);  // AND_Gate
  and _111 (_111_out, d_ff_1_q, d_ff_2_q, d_ff_3_q, State);
  or or_1 (R1, _000_out, _110_out, _001_out, _100_out, _101_out);
  D_Flip_Flop d_ff_1 (.clk(Clock), .D(d_ff_4_q), .Q(d_ff_1_q));  // open: Qn, preset, en, reset
  D_Flip_Flop d_ff_2 (.clk(Clock), .D(d_ff_5_q), .Q(d_ff_2_q));  // open: Qn, preset, en, reset
  D_Flip_Flop d_ff_3 (.clk(Clock), .D(d_ff_6_q), .Q(d_ff_3_q));  // open: Qn, preset, en, reset
  not not_1 (not_1_out, Clock);
  buf or_2 (Y1, _011_out);  // OR_Gate
  D_Flip_Flop d_ff_4 (.clk(not_1_out), .D(or_4_out), .Q(d_ff_4_q));  // open: Qn, preset, en, reset
  D_Flip_Flop d_ff_5 (.clk(not_1_out), .D(or_5_out), .Q(d_ff_5_q));  // open: Qn, preset, en, reset
  D_Flip_Flop d_ff_6 (.clk(not_1_out), .D(or_6_out), .Q(d_ff_6_q));  // open: Qn, preset, en, reset
  or or_3 (G1, _010_out, _111_out);
  or or_4 (or_4_out, _110_out, _101_out, _100_out, _011_out);
  or or_5 (or_5_out, _001_out, _010_out, _101_out, _110_out);
  or or_6 (or_6_out, _010_out, _110_out, _000_out, _100_out);
  or or_7 (Y2, _001_out, _101_out);
  or or_8 (R2, _111_out, _010_out, _011_out, _110_out);
  or or_9 (G2, _000_out, _100_out);

  // Notes on the sheet:
  //   X
  //   0
  //   0
  //   X
  //   1
  //   1
  //   1
  //   1
  //   S2
  //   S1
  //   S0
  //   S2'
  //   S1'
  //   S0'
endmodule
